# Fritzing sketch LEGObuilderHardware (saved by Fritzing 0.8.7b)

parts:
  Raspberry_Pi_B_rev1 = Raspberry Pi B rev2
  Delta_Motor_3 = Basic Servo
  PWM1 = PCA9685 16x12-bit PWM Breakout
  Delta_Traversal = Stepper Motor - Unipolar
  Delta_Motor_2 = Basic Servo
  Delta_Motor_1 = Basic Servo
  Gripper_Pitch = Basic Servo
  Gripper_Open/Close = Basic Servo
  Camera = Rasberry Pi NIOR Camera [chip_label=IC package="DIP (Dual Inline) [THT]"]  # not connected
  Delta_Rotation = Stepper Motor - Unipolar

nets:
  N1: Raspberry_Pi_B_rev1.GPIO_2, PWM1.no_name_yet#504
  N2: Raspberry_Pi_B_rev1.GPIO_3, PWM1.no_name_yet#503
  GND: Delta_Motor_3.gnd, PWM1.no_name_yet#1000, PWM1.no_name_yet#1001, PWM1.no_name_yet#1008, PWM1.no_name_yet#1009, PWM1.no_name_yet#1010, PWM1.no_name_yet#1012, PWM1.no_name_yet#1013, PWM1.no_name_yet#1014, PWM1.no_name_yet#1015, Delta_Traversal.C, Delta_Traversal.D, Delta_Motor_2.gnd, Delta_Motor_1.gnd, Gripper_Pitch.gnd, Gripper_Open/Close.gnd, Delta_Rotation.C, Delta_Rotation.D
  VCC: Delta_Motor_3.vcc, PWM1.no_name_yet#100, PWM1.no_name_yet#101, PWM1.no_name_yet#108, PWM1.no_name_yet#109, PWM1.no_name_yet#110, PWM1.no_name_yet#112, PWM1.no_name_yet#113, PWM1.no_name_yet#114, PWM1.no_name_yet#115, Delta_Traversal.A, Delta_Traversal.B, Delta_Motor_2.vcc, Delta_Motor_1.vcc, Gripper_Pitch.vcc, Gripper_Open/Close.vcc, Delta_Rotation.A, Delta_Rotation.B
  N3: Delta_Motor_3.pulse, PWM1.no_name_yet#8
  N4: PWM1.no_name_yet#0, Gripper_Pitch.pulse
  N5: PWM1.no_name_yet#1, Gripper_Open/Close.pulse
  N6: PWM1.no_name_yet#9, Delta_Motor_2.pulse
  N7: PWM1.no_name_yet#10, Delta_Motor_1.pulse
  N8: PWM1.no_name_yet#12, Delta_Traversal.COMMON_2
  N9: PWM1.no_name_yet#13, Delta_Traversal.COMMON_1
  N10: PWM1.no_name_yet#14, Delta_Rotation.COMMON_2
  N11: PWM1.no_name_yet#15, Delta_Rotation.COMMON_1

custom parts:
  Rasberry Pi NIOR Camera: Camera
